# Fritzing sketch etch-a-sketch_v2 (saved by Fritzing 0.9.4)
breadboards: 1

parts:
  Argon1 = Particle Argon
  S1 = Pushbutton [package="[THT]"]
  R1 = Resistor [tolerance=±5% resistance=10k package=THT]
  R2 = TRIMPOT [package=3362u-2]
  R3 = TRIMPOT [package=3362u-2]
  Qwiic_OLED_Breakout2 = Qwiic_OLED_Breakout  # not connected

nets:
  N1: Argon1.3.3V, R1.Pin_1, R2.CW, R3.CW
  N2: Argon1.GND, S1.Pin_1, S1.Pin_2, R2.CCW, R3.CCW
  N3: Argon1.A0, R3.WIPER
  N4: Argon1.A1, R2.WIPER
  N5: Argon1.D2, S1.Pin_3, S1.Pin_4, R1.Pin_0

notes:
  OLED
  Use Qwiic cable

custom parts:
  Particle Argon: The Argon is a powerful Wi-Fi enabled development board that can act as either a standalone Wi-Fi endpoint or Wi-Fi enabled gateway for Particle Mesh networks. It is based on the Nordic nRF52840 and has built-in battery charging circuitry so it’s easy to connect a Li-Po and deploy your local network in minutes. The Argon is great for connecting existing projects to the Particle Device Cloud or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
  Qwiic_OLED_Breakout: The SparkFun Qwiic Micro OLED Breakout is a Qwiic-enabled version of our popular Micro OLED display! The small monochrome, blue-on-black OLED screen presents incredibly clear images for your viewing pleasure. It’s “micro,” but it still packs a punch --- the OLED display is crisp, and you can fit a deceivingly large amount of graphics on there. This breakout is perfect for adding graphics to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
