# Fritzing sketch led_pot (saved by Fritzing 0.9.4)
breadboards: 1

parts:
  R1 = Resistor [tolerance=±5% resistance=330 package=THT]
  Argon2 = Particle Argon
  R7 = TRIMPOT [package=3362u-2]
  LED2 = LED - 5mm [color="Red (633nm)" package="5 mm [THT]"]

nets:
  N1: R1.Pin_0, LED2.anode
  N2: R1.Pin_1, Argon2.D2
  N3: Argon2.3.3V, R7.CCW
  N4: Argon2.GND, R7.CW, LED2.cathode
  N5: Argon2.A0, R7.WIPER

custom parts:
  Particle Argon: The Argon is a powerful Wi-Fi enabled development board that can act as either a standalone Wi-Fi endpoint or Wi-Fi enabled gateway for Particle Mesh networks. It is based on the Nordic nRF52840 and has built-in battery charging circuitry so it’s easy to connect a Li-Po and deploy your local network in minutes. The Argon is great for connecting existing projects to the Particle Device Cloud or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
