# Fritzing sketch button_latch_two_leds (saved by Fritzing 0.9.4)
breadboards: 1

parts:
  S2 = Pushbutton [package="[THT]"]
  R1 = Resistor [tolerance=±5% resistance=10k package=THT]
  Argon4 = Particle Argon
  LED1 = LED - 5mm [color="Blue (470nm)" package="5 mm [THT]"]
  LED2 = LED - 5mm [color="Green (570nm)" package="5 mm [THT]"]
  R2 = Resistor [tolerance=±5% resistance=330 package=THT]
  R3 = Resistor [tolerance=±5% resistance=330 package=THT]

nets:
  N1: S2.Pin_1, S2.Pin_2, R1.Pin_0, Argon4.RESET
  N2: S2.Pin_3, S2.Pin_4, R1.Pin_1, Argon4.D2
  N3: Argon4.GND, R2.Pin_0, R3.Pin_0
  N4: Argon4.D3, LED2.anode
  N5: Argon4.D4, LED1.anode
  N6: LED1.cathode, R3.Pin_1
  N7: LED2.cathode, R2.Pin_1

custom parts:
  Particle Argon: The Argon is a powerful Wi-Fi enabled development board that can act as either a standalone Wi-Fi endpoint or Wi-Fi enabled gateway for Particle Mesh networks. It is based on the Nordic nRF52840 and has built-in battery charging circuitry so it’s easy to connect a Li-Po and deploy your local network in minutes. The Argon is great for connecting existing projects to the Particle Device Cloud or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
