# Fritzing sketch correct_pullup_button_wiring (saved by Fritzing 0.9.3b)
breadboards: 3

parts:
  S1 = Pushbutton [package="[THT]"]
  Argon1 = Particle Argon
  S2 = Pushbutton [package="[THT]"]
  Argon2 = Particle Argon
  R1 = Resistor [tolerance=±5% resistance=10k package=THT]
  S3 = Pushbutton [package="[THT]"]
  Argon3 = Particle Argon

nets:
  N1: S1.Pin_1, S1.Pin_2, Argon1.GND
  N2: S1.Pin_3, S1.Pin_4, Argon1.3.3V, Argon1.D2
  N3: S2.Pin_1, S2.Pin_2, Argon2.GND
  N4: S2.Pin_3, S2.Pin_4, Argon2.D2, R1.Pin_1
  N5: Argon2.3.3V, R1.Pin_0
  N6: S3.Pin_1, S3.Pin_2, Argon3.GND
  N7: S3.Pin_3, S3.Pin_4, Argon3.D2

custom parts:
  Particle Argon: The Argon is a powerful Wi-Fi enabled development board that can act as either a standalone Wi-Fi endpoint or Wi-Fi enabled gateway for Particle Mesh networks. It is based on the Nordic nRF52840 and has built-in battery charging circuitry so it’s easy to connect a Li-Po and deploy your local network in minutes. The Argon is great for connecting existing projects to the Particle Device Cloud or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
