# Fritzing sketch rgb_led_button (saved by Fritzing 0.9.10b)
breadboards: 1

parts:
  R1 = Resistor [tolerance=±5% resistance=330 power=0.25 package=THT]
  LED1 = RGB LED (com. cathode, rgb) [package="5 mm [THT]"]
  R4 = Resistor [tolerance=±5% resistance=330 power=0.25 package=THT]
  R5 = Resistor [tolerance=±5% resistance=330 power=0.25 package=THT]
  S3 = Pushbutton [package="[THT]"]
  R6 = Resistor [tolerance=±5% resistance=10k power=0.25 package=THT]
  A1 = Particle Photon 2

nets:
  N1: R1.Pin_0, LED1.red_anode
  N2: R1.Pin_1, A1.Pin_18
  N3: LED1.common_cathode, S3.Pin_1, S3.Pin_2, A1.Pin_4, A1.Pin_30
  N4: LED1.green_anode, R4.Pin_0
  N5: LED1.blue_anode, R5.Pin_0
  N6: R4.Pin_1, A1.Pin_13
  N7: R5.Pin_1, A1.Pin_12
  N8: S3.Pin_3, S3.Pin_4, R6.Pin_1, A1.Pin_22
  N9: R6.Pin_0, A1.Pin_2
  N10: A1.Pin_28, A1.Pin_29

custom parts:
  Particle Photon 2: The Photon 2 is a development module with a microcontroller and Wi-Fi networking. -- This Fritzing file originally created by Peter Van Epp https://forum.fritzing.org/t/request-particle-photon2/19824/2 5/18/2024 - Rob Parke Rotated breadboard image
