# Fritzing sketch rgb_led_common_anode (saved by Fritzing 0.9.10b)
breadboards: 1

parts:
  R11 = Resistor [tolerance=±5% resistance=330 power=0.25 package=THT]
  R12 = Resistor [tolerance=±5% resistance=330 power=0.25 package=THT]
  R13 = Resistor [tolerance=±5% resistance=330 power=0.25 package=THT]
  LED3 = RGB LED (com. cathode, rgb) [package="5 mm [THT]"]
  A2 = Particle Photon 2

nets:
  N1: R11.Pin_0, LED3.red_anode
  N2: R11.Pin_1, A2.Pin_18
  N3: R12.Pin_0, LED3.green_anode
  N4: R12.Pin_1, A2.Pin_13
  N5: R13.Pin_0, LED3.blue_anode
  N6: R13.Pin_1, A2.Pin_12
  N7: LED3.common_cathode, A2.Pin_2
  N8: A2.Pin_4, A2.Pin_30
  N9: A2.Pin_28, A2.Pin_29

custom parts:
  Particle Photon 2: The Photon 2 is a development module with a microcontroller and Wi-Fi networking. -- This Fritzing file originally created by Peter Van Epp https://forum.fritzing.org/t/request-particle-photon2/19824/2 5/18/2024 - Rob Parke Rotated breadboard image
