# Fritzing sketch rgb_led_switch (saved by Fritzing 0.9.10b)
breadboards: 1

parts:
  A2 = Particle Photon 2
  S2 = Toggle Switch [package=THT]
  R13 = Resistor [tolerance=±5% resistance=330 power=0.25 package=THT]
  R14 = Resistor [tolerance=±5% resistance=330 power=0.25 package=THT]
  R15 = Resistor [tolerance=±5% resistance=330 power=0.25 package=THT]
  LED4 = RGB LED (com. cathode, rgb) [package="5 mm [THT]"]

nets:
  N1: A2.Pin_2, S2.L1
  N2: A2.Pin_4, A2.Pin_30, S2.L2, LED4.common_cathode
  N3: A2.Pin_10, S2.COM
  N4: A2.Pin_12, R15.Pin_1
  N5: A2.Pin_13, R14.Pin_1
  N6: A2.Pin_18, R13.Pin_1
  N7: A2.Pin_28, A2.Pin_29
  N8: R13.Pin_0, LED4.red_anode
  N9: R14.Pin_0, LED4.green_anode
  N10: R15.Pin_0, LED4.blue_anode

custom parts:
  Particle Photon 2: The Photon 2 is a development module with a microcontroller and Wi-Fi networking. -- This Fritzing file originally created by Peter Van Epp https://forum.fritzing.org/t/request-particle-photon2/19824/2 5/18/2024 - Rob Parke Rotated breadboard image
