# Fritzing sketch stoplight_RGB_OLED (saved by Fritzing 0.9.10b)
breadboards: 1

parts:
  R6 = Resistor [tolerance=±5% resistance=330 power=0.25 package=THT]
  LED2 = RGB LED (com. cathode, rgb) [package="5 mm [THT]"]
  R7 = Resistor [tolerance=±5% resistance=330 power=0.25 package=THT]
  R8 = Resistor [tolerance=±5% resistance=330 power=0.25 package=THT]
  Qwiic_OLED_Breakout3 = Qwiic_OLED_Breakout  # not connected
  A1 = Particle Photon 2

nets:
  N1: R6.Pin_0, LED2.red_anode
  N2: R6.Pin_1, A1.Pin_7
  N3: LED2.common_cathode, A1.Pin_4, A1.Pin_30
  N4: LED2.green_anode, R7.Pin_0
  N5: LED2.blue_anode, R8.Pin_0
  N6: R7.Pin_1, A1.Pin_8
  N7: R8.Pin_1, A1.Pin_12
  N8: A1.Pin_28, A1.Pin_29

notes:
  NorthSouth Signal
  Walk/Don't Walk
  use Qwiic cable

custom parts:
  Qwiic_OLED_Breakout: The SparkFun Qwiic Micro OLED Breakout is a Qwiic-enabled version of our popular Micro OLED display! The small monochrome, blue-on-black OLED screen presents incredibly clear images for your viewing pleasure. It’s “micro,” but it still packs a punch --- the OLED display is crisp, and you can fit a deceivingly large amount of graphics on there. This breakout is perfect for adding graphics to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
  Particle Photon 2: The Photon 2 is a development module with a microcontroller and Wi-Fi networking. -- This Fritzing file originally created by Peter Van Epp https://forum.fritzing.org/t/request-particle-photon2/19824/2 5/18/2024 - Rob Parke Rotated breadboard image
