# Fritzing sketch servo_dc_fan_controller (saved by Fritzing 0.9.4)
breadboards: 2

parts:
  Part1 = Motor Driver 1A Dual TB6612FNG  # not connected
  Argon1 = Particle Argon
  M1 = DC Motor  # not connected
  J2 = Basic Servo
  R1 = TRIMPOT [package=3362u-2]

nets:
  N1: Argon1.3.3V, R1.CCW
  GND: Argon1.GND, J2.gnd, R1.CW
  N2: Argon1.A0, R1.WIPER
  N3: Argon1.D2, J2.pulse
  N4: Argon1.VUSB, J2.vcc

custom parts:
  Particle Argon: The Argon is a powerful Wi-Fi enabled development board that can act as either a standalone Wi-Fi endpoint or Wi-Fi enabled gateway for Particle Mesh networks. It is based on the Nordic nRF52840 and has built-in battery charging circuitry so it’s easy to connect a Li-Po and deploy your local network in minutes. The Argon is great for connecting existing projects to the Particle Device Cloud or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
