# Fritzing sketch oled and ultrasonic i2c (saved by Fritzing 0.9.10b)
breadboards: 1

parts:
  HC-SR04_Sensor_1 = HC-SR04 Ultrasonic Distance Sensor
  Qwiic_OLED_Breakout1 = Qwiic_OLED_Breakout  # not connected
  A1 = Particle Photon 2

nets:
  N1: HC-SR04_Sensor_1.VCC, A1.Pin_26
  N2: HC-SR04_Sensor_1.TRIG, A1.Pin_23
  N3: HC-SR04_Sensor_1.ECHO, A1.Pin_22
  N4: HC-SR04_Sensor_1.GND, A1.Pin_4, A1.Pin_30
  N5: A1.Pin_28, A1.Pin_29

notes:
  Use Qwiic
  cable

custom parts:
  Qwiic_OLED_Breakout: The SparkFun Qwiic Micro OLED Breakout is a Qwiic-enabled version of our popular Micro OLED display! The small monochrome, blue-on-black OLED screen presents incredibly clear images for your viewing pleasure. It’s “micro,” but it still packs a punch --- the OLED display is crisp, and you can fit a deceivingly large amount of graphics on there. This breakout is perfect for adding graphics to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
  Particle Photon 2: The Photon 2 is a development module with a microcontroller and Wi-Fi networking. -- This Fritzing file originally created by Peter Van Epp https://forum.fritzing.org/t/request-particle-photon2/19824/2 5/18/2024 - Rob Parke Rotated breadboard image
