# Fritzing sketch rfid (saved by Fritzing 0.9.10b)
breadboards: 1

parts:
  Part1 = RFID-RC522-v2
  A1 = Particle Photon 2

nets:
  N1: Part1.SDA, A1.Pin_5
  N2: Part1.SCK, A1.Pin_11
  N3: Part1.MOSI, A1.Pin_12
  N4: Part1.MISO, A1.Pin_13
  N5: Part1.GND, A1.Pin_4, A1.Pin_30
  N6: Part1.RST, A1.Pin_6
  N7: Part1.3.3V, A1.Pin_2, A1.Pin_31
  N8: A1.Pin_28, A1.Pin_29

custom parts:
  RFID-RC522-v2: A simple China made RFID-RC522 Reader; do check the pin labels, as this is a MFRC522 based clone.
  Particle Photon 2: The Photon 2 is a development module with a microcontroller and Wi-Fi networking. -- This Fritzing file originally created by Peter Van Epp https://forum.fritzing.org/t/request-particle-photon2/19824/2 5/18/2024 - Rob Parke Rotated breadboard image
