# Fritzing sketch open_pir_sparkfun (saved by Fritzing 0.9.4)
breadboards: 1

parts:
  Part7 = HC-SR501 Body Sensor Module
  Argon1 = Particle Argon

nets:
  VCC: Part7.VCC, Argon1.3.3V
  N1: Part7.GND, Argon1.D2

notes:
  Note Sparkfun OpenPIR looks different

custom parts:
  HC-SR501 Body Sensor Module: Pyroelectric Infrared PIR Motion Sensor Detector Module
  Particle Argon: The Argon is a powerful Wi-Fi enabled development board that can act as either a standalone Wi-Fi endpoint or Wi-Fi enabled gateway for Particle Mesh networks. It is based on the Nordic nRF52840 and has built-in battery charging circuitry so it’s easy to connect a Li-Po and deploy your local network in minutes. The Argon is great for connecting existing projects to the Particle Device Cloud or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
