# Fritzing sketch sleep_wake_button (saved by Fritzing 0.9.10b)
breadboards: 1

parts:
  S1 = Momentary Switch [package=ksa_sealed_tac_switch]
  R1 = Resistor [tolerance=±5% resistance=10k power=0.25 package=THT]
  A1 = Particle Photon 2

nets:
  N1: S1.2, A1.Pin_4, A1.Pin_30
  N2: S1.3, A1.Pin_25
  N3: S1.4, R1.Pin_0
  N4: R1.Pin_1, A1.Pin_2
  N5: A1.Pin_28, A1.Pin_29

custom parts:
  Particle Photon 2: The Photon 2 is a development module with a microcontroller and Wi-Fi networking. -- This Fritzing file originally created by Peter Van Epp https://forum.fritzing.org/t/request-particle-photon2/19824/2 5/18/2024 - Rob Parke Rotated breadboard image
