# Fritzing sketch dht22 (saved by Fritzing 0.9.10b)
breadboards: 1

parts:
  DHT_1 = DHT20 Humidity and Temperature Sensor
  A1 = Particle Photon 2

nets:
  N1: DHT_1.VDD, A1.Pin_2, A1.Pin_31
  N2: DHT_1.SDA, A1.Pin_17
  N3: DHT_1.GND, A1.Pin_4, A1.Pin_30
  N4: DHT_1.SCL, A1.Pin_18
  N5: A1.Pin_28, A1.Pin_29

custom parts:
  Particle Photon 2: The Photon 2 is a development module with a microcontroller and Wi-Fi networking. -- This Fritzing file originally created by Peter Van Epp https://forum.fritzing.org/t/request-particle-photon2/19824/2 5/18/2024 - Rob Parke Rotated breadboard image
